# Fritzing sketch oLED (saved by Fritzing 0.9.2b)
breadboards: 1

parts:
  U1 = Barometric Pressure Sensor
  Part1 = Arduino Uno (Rev3)

nets:
  N1: U1.DRDY, Part1.D12/MISO
  N2: U1.CSB, Part1.D11_PWM/MOSI
  N3: U1.MISO, Part1.D13/SCK
  N4: U1.MOSI, Part1.D9_PWM
  N5: U1.SCK, Part1.D10_PWM/SS
  3.3V: U1.3.3V, Part1.5V
  GND: U1.GND, Part1.GND
